# Fritzing sketch OpenerPcr (saved by Fritzing 0.7.10b)
breadboards: 2

parts:
  Arduino1 = Arduino
  LCD1 = LCD screen  # not connected
  J1 = Peltier Element
  K1 = Relay [part_number=FRS1B-S package=THT]
  K2 = Relay [part_number=FRS1B-S package=THT]
  K3 = Relay [part_number=FRS1B-S package=THT]
  K4 = Relay [part_number=FRS1B-S package=THT]
  T1 = Temperature Sensor (Thermistor) [thermistor_type=NTC package=THT]
  T2 = Temperature Sensor (Thermistor) [thermistor_type=NTC package=THT]
  R1 = Resistor [tolerance=±5% resistance=220 package=THT]
  R2 = Resistor [tolerance=±5% resistance=220 package=THT]
  R3 = Resistor [tolerance=±5% resistance=220 package=THT]
  R4 = Resistor [tolerance=±5% resistance=220 package=THT]
  Power_plug1 = Power plug [part_number="Power supply"]
  R5 = Resistor [tolerance=±5% resistance=0 part_number="Heating element" package=THT]
  K5 = Relay [part_number=FRS1B-S package=THT]
  R6 = Resistor [tolerance=±5% resistance=220 package=THT]
  Arduino2 = Arduino

nets:
  N1: Arduino1.D2, K1.COIL2
  N2: Arduino1.+5V, R1.Pin_0, R3.Pin_0
  N3: Arduino1.GND, R2.Pin_1, R4.Pin_1, R6.Pin_1
  N4: J1.pin1, K3.B
  N5: J1.pin2, K2.B
  N6: K1.A, R5.Pin_0
  N7: K1.COIL1, R6.Pin_0
  N8: K1.C1, K1.C2
  N9: K1.B, K4.B, Power_plug1.GND, K5.B
  N10: K2.A, K3.A, Power_plug1.VCC, R5.Pin_1
  N11: K2.COIL1, K3.COIL1, K4.COIL1, K5.COIL1, Arduino2.GND
  N12: K2.C1, K2.C2
  N13: K2.COIL2, K5.COIL2, Arduino2.D6
  N14: K3.C1, K3.C2
  N15: K3.COIL2, K4.COIL2, Arduino2.D0RX
  N16: K4.C1, K4.C2
  N17: T1.pin_1, R3.Pin_1, R4.Pin_0
  N18: T2.pin_1, R1.Pin_1, R2.Pin_0
  N19: K5.C1, K5.C2

notes:
  H brug: allow for switching the current direction
  2 pins
  Heating element
  1 pin
  LCD: program will be put it by software
  5 pins (not shown)
  2 thermistors
  Determine resistor values by experiment
  1 pin each
  Our external power supply
  Switching of relay
  1 per relay
  Will need five
  1 pin each
  With two pins
  the direction of
  current is controlled
  Relays need
  rectifier diodes.
  Add it later
  (not shown)
  Use only one Arduino: I copied it for better clarity of the circuit. The pin
  number on the Arduino are chosen based on clarity and will not be the
  real pin numbers
