# Fritzing sketch OpenerPcrTask2 (saved by Fritzing 0.8.0b)
breadboards: 1

parts:
  Arduino1 = Arduino
  K1 = Relay [part_number=FRS1B-S package=THT]
  LED1 = LED - 5mm [color="Red (633nm)" package="5 mm [THT]"]
  R_led = Resistor [tolerance=±5% resistance=100 package=THT]
  R_control = Resistor [tolerance=±5% resistance=22 package=THT]

nets:
  N1: Arduino1.D2, K1.COIL2
  N2: Arduino1.+5V, R_led.Pin_1
  N3: Arduino1.GND, K1.B, R_control.Pin_1
  N4: K1.C1, K1.C2, LED1.cathode
  N5: LED1.anode, R_led.Pin_0

notes:
  I read that relays need
  rectifier diodes.
  Is this so (Google)? If yes, add it to the schematic
  This should be a multimeter, set to
  10 VDC
  When the frequency increases, the voltage might increase! This might damage the Arduino. Stop increasing the frequency when you notice this!
  f = 20 Hz
  The LED will burn if the relay is closed due to current from Arduino pin 2
  R_led = 100 ohm
  The relay switching port must be connected to ground with a resistance (otherwise it will short-circuit). Try to find the resistance with the highest possible value that yields reliable switching
  R_control = 22 ohm
  #include <assert.h>
  const int pin = 2; // digital pin number 2
  void setup()
  {
  setPin(pin,OUTPUT)
  }
  void loop()
  {
  const double frequency = 1.0; //Change this
  assert(frequency != 0.0);
  const double period = 1.0 / frequency;
  digitalWrite(pin,HIGH);
  delay(period);
  digitalWrite(pin,LOW);
  delay(period);
  }
  OpenPCR task 2: find out the maximum switching frequency of the relay
  f = 20 Hz. Increasing this will change the click-click-sound to a crrrrrrr-sound
