# Fritzing sketch OpenerPcrTask3 (saved by Fritzing 0.8.0b)
breadboards: 1

parts:
  J1 = Peltier Element
  J2 = shrouded pin header, 20 pins [form="♂ (shrouded male)"]

nets:
  N1: J1.pin1, J2.pin18
  N2: J1.pin2, J2.pin10
  N3: J2.pin16, J2.pin17

notes:
  External power supply
  Pin bottom left = +12 VDC
  Pin top left = GND
  Check this!
  The orange connection will make the fan turn (upper pin = PS_ON, lower pin = GND)
  Which resistor to use here?
  None :)
  This side is side B. It will cool.
