# Fritzing sketch TicTacToeMachine (saved by Fritzing 0.8.0b)
breadboards: 3

parts:
  R_in_3 = Resistor [tolerance=±5% resistance=10k package=THT]
  R_in_2 = Resistor [tolerance=±5% resistance=10k package=THT]
  R_in_1 = Resistor [tolerance=±5% resistance=10k package=THT]
  R_out = Resistor [tolerance=±5% resistance=100 package=THT]
  CMOS_1 = mystery part, 14 pins [chip_label="CMOS4073 (3AND)"]
  Led_out = LED - 5mm [color="Infrared (940nm)" package="5 mm [THT]"]
  VCC1 = 4 x AAA Battery Mount
  S2 = Pushbutton [package=THT]
  S3 = Pushbutton [package=THT]
  S4 = Pushbutton [package=THT]
  LED1 = LED - 5mm [color="Red (633nm)" package="5 mm [THT]"]
  B_red = LED - 5mm [color="Red (633nm)" package="5 mm [THT]"]
  LED3 = LED - 5mm [color="Red (633nm)" package="5 mm [THT]"]
  R_A_Red = Resistor [tolerance=±5% resistance=100 package=THT]
  R_B_red = Resistor [tolerance=±5% resistance=100 package=THT]
  R3 = Resistor [tolerance=±5% resistance=100 package=THT]
  Led_out1 = LED - 5mm [color="Red (633nm)" package="5 mm [THT]"]
  CMOS_2 = mystery part, 14 pins [chip_label=4OR]
  R_in_4 = Resistor [tolerance=±5% resistance=10k package=THT]
  R_in_5 = Resistor [tolerance=±5% resistance=10k package=THT]
  R_out1 = Resistor [tolerance=±5% resistance=100 package=THT]

nets:
  N1: R_in_3.Pin_0, R_in_2.Pin_0, R_in_1.Pin_0, CMOS_1.pin7, Led_out.cathode, VCC1.-, R_A_Red.Pin_1, R_B_red.Pin_1, R3.Pin_1, Led_out1.cathode, CMOS_2.pin7, R_in_4.Pin_0, R_in_5.Pin_0
  N2: R_in_3.Pin_1, CMOS_1.pin5, S4.leg0, LED3.cathode
  N3: R_in_2.Pin_1, CMOS_1.pin4, S3.leg0, B_red.cathode
  N4: R_in_1.Pin_1, CMOS_1.pin3, S2.leg0, LED1.cathode
  N5: R_out.Pin_0, Led_out.anode
  N6: R_out.Pin_1, CMOS_1.pin6, CMOS_2.pin1
  N7: CMOS_1.pin1, VCC1.+, S2.leg1, S3.leg1, S4.leg1, CMOS_2.pin14
  N8: LED1.anode, R_A_Red.Pin_0
  N9: B_red.anode, R_B_red.Pin_0
  N10: LED3.anode, R3.Pin_0
  N11: Led_out1.anode, R_out1.Pin_0
  N12: CMOS_2.pin3, R_out1.Pin_1

notes:
  These aren't real pushbuttons:
  Their connections are closed when the red player is one places A B and/or C
  This LED indicates that player red has gotten three in a row on the top horizontal row
  This section handles
  1) The power for each individual arena LED's
  2) passes the arena's state to the next
  This section handles:
  1) Detection if a player has gotten three in a row
  2) If yes, passes it to the next section
  This LED indicates that player red has three in a row
  This section handles the display of a player having three in a row
  Each connection from below goes to two or three 3AND ports in the section below
  Per player there will be 8 connection from the upper section the the lower section
